# Fritzing sketch garage (saved by Fritzing 1.0.5)
perfboards: 1

parts:
  IR_Transmitter = LED - 5mm [color="Infrared (940nm)" current=0.030A package="5 mm [THT]"]
  IR_Receiver = mystery part, 4 pins [chip_label="IR Receiver"]
  Lichtschranke = Basic FET P-Channel [package="TO220 [THT]"]
  Mod1 = Raspberry Pi 4B  # not connected
  Tor_auf = SWITCH-MOMENTARY-2 [package=tactile-switch-1101ne]
  Tor_zu = SWITCH-MOMENTARY-2 [package=tactile-switch-1101ne]
  IR_Scheinwerfer = LED - 3mm [color="Infrared (940nm)" current=0.030A package="3 mm [THT]"]
  Scheinwerfer = Basic FET P-Channel [package="TO220 [THT]"]
  Netzteil = DC Power [voltage=12V internal_resistance=0.1Ω]
  Tor_auf_2 = Camdenboss CTB0158-2 [part_number=CTB0158-2 package=THT]
  J1 = Raspberry Pi Header 40pin [form="♂ (male)" package=THT]
  Tor_zu_2 = Camdenboss CTB0158-2 [part_number=CTB0158-2 package=THT]
  Lichtschranke_Strom = Camdenboss CTB0158-2 [part_number=CTB0158-2 package=THT]
  IR_Signal = Camdenboss CTB0158-2 [part_number=CTB0158-2 package=THT]
  IR_Scheinwerfer_Strom = Camdenboss CTB0158-2 [part_number=CTB0158-2 package=THT]
  12V_in = Camdenboss CTB0158-2 [part_number=CTB0158-2 package=THT]
  Tor_Motor = Camdenboss CTB0158-2 [part_number=CTB0158-2 package=THT]
  Tor = Basic FET P-Channel [package="TO220 [THT]"]
  Bauteil1 = 12 NeoPixel Ring [part_number=1643]
  LED = Camdenboss CTB0158-2 [part_number=CTB0158-2 package=THT]

nets:
  N1: IR_Transmitter.cathode, IR_Receiver.pin2, Lichtschranke_Strom.terminal_2
  N2: IR_Transmitter.anode, IR_Receiver.pin1, Lichtschranke_Strom.terminal_1
  N3: IR_Receiver.pin3, IR_Signal.terminal_1
  N4: IR_Receiver.pin4, IR_Signal.terminal_2
  N5: Lichtschranke.gate, J1.GIPO26
  N6: Lichtschranke.drain, Lichtschranke_Strom.pin2
  GND: Lichtschranke.source, Scheinwerfer.source, J1.GND, 12V_in.pin2, Tor_Motor.pin2, Tor.source, Bauteil1.GND
  N7: Tor_auf.1, Tor_auf_2.terminal_1
  N8: Tor_auf.2, Tor_auf_2.terminal_2
  N9: Tor_zu.1, Tor_zu_2.terminal_1
  N10: Tor_zu.2, Tor_zu_2.terminal_2
  N11: IR_Scheinwerfer.cathode, IR_Scheinwerfer_Strom.terminal_2
  N12: IR_Scheinwerfer.anode, IR_Scheinwerfer_Strom.terminal_1
  N13: Scheinwerfer.gate, J1.GIPO19
  N14: Scheinwerfer.drain, IR_Scheinwerfer_Strom.pin2
  N15: Netzteil.V-, 12V_in.terminal_2
  N16: Netzteil.V+, 12V_in.terminal_1
  3V3: Tor_auf_2.pin1, J1.3v3, J1.3V3, Tor_zu_2.pin1, IR_Signal.pin1
  N17: Tor_auf_2.pin2, J1.GIPO17
  N18: J1.GIPO27, Tor_zu_2.pin2
  N19: J1.GIPO22, IR_Signal.pin2
  N20: J1.GIPO10, LED.pin2
  N21: J1.GIPO13, Tor.gate
  N22: J1.5V, LED.pin1
  N23: Lichtschranke_Strom.pin1, IR_Scheinwerfer_Strom.pin1, 12V_in.pin1
  N24: Tor_Motor.pin1, Tor.drain
  N25: Bauteil1.IN, LED.terminal_2
  N26: Bauteil1.VDD, LED.terminal_1

custom parts:
  Raspberry Pi Header 40pin: Raspberry Pi 40 pin header - for creating your own shields.
  12 NeoPixel Ring: 12 ultra bright smart LED NeoPixels are arranged in a circle with 1.5" (37mm) outer diameter. The rings are 'chainable' - connect the output pin of one to the input pin of another. Use only one microcontroller pin to control as many as you can chain together! Each LED is addressable as the driver chip is inside the LED. Each one has ~18mA constant current drive so the color will be very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
